// Logisim project TestFile.circ as structural Verilog: 1 circuit, main circuit main
module main (
  input  in_1,
  input  in_2,
  input  in_3,
  input  in_4
);

  wire adder_1_cout, undriven_3;
  wire [7:0] adder_1_out;
  wire [7:1] undriven, undriven_2;

  Adder adder_1 (
    .a({undriven, in_1}), .b({undriven_2, in_3}), .out(adder_1_out), .cin(undriven_3), .cout(adder_1_cout));
  D_Flip_Flop d_ff_1 ();  // open: clk, D, Q, Qn, preset, en, reset
  D_Flip_Flop d_ff_2 ();  // open: clk, D, Q, Qn, preset, en, reset
  D_Flip_Flop d_ff_3 ();  // open: clk, D, Q, Qn, preset, en, reset
  D_Flip_Flop d_ff_4 ();  // open: clk, D, Q, Qn, preset, en, reset
  // Pins of 1 and 8 bits meet at {undriven, in_1}
  // Pins of 1 and 8 bits meet at {undriven_2, in_3}
endmodule
